# Fritzing sketch key_pad_door_lock (saved by Fritzing 0.9.10b)
breadboards: 1

parts:
  Part1 = Arduino Ethernet Shield (Rev3)
  BAT1 = BC9VPC [package=bc9vpc]
  Keypad4x1 = Membran Keypad 4x4
  Part2 = KY-019 5V Relay Module [package="Breakout board"]
  L1 = Solenoid
  LCM1602_IIC1 = LCM1602 IIC [part_number="LCM1602 IIC" chip_label="LCM1602 IIC" package="DIP (Dual Inline) [THT]"]
  LCD1 = LCD screen

nets:
  N1: Part1.D8, Keypad4x1.Pin7
  N2: Part1.PWM_D9, Keypad4x1.Pin8
  N3: Part1.PWM_D11, Part2.S
  GND: Part1.GND, BAT1.V-, Part2.-, L1.pin1, LCM1602_IIC1.GND
  N4: Part1.A4/SDA, LCM1602_IIC1.SDA
  N5: Part1.A5/SCL, LCM1602_IIC1.SCL
  N6: Part1.D2, Keypad4x1.Pin1
  N7: Part1.PWM_D3, Keypad4x1.Pin2
  N8: Part1.SDCS, Keypad4x1.Pin3
  N9: Part1.PWM_D5, Keypad4x1.Pin4
  N10: Part1.PWM_D6, Keypad4x1.Pin5
  N11: Part1.D7, Keypad4x1.Pin6
  5V: Part1.5V, Part2.+, LCM1602_IIC1.VCC
  N12: BAT1.V+, Part2.NC
  N13: Part2.Common, L1.pin2
  VSS: LCM1602_IIC1.VSS, LCD1.VSS
  VDD: LCM1602_IIC1.VDD, LCD1.VDD
  N14: LCM1602_IIC1.V0, LCD1.V0
  N15: LCM1602_IIC1.RS, LCD1.RS
  N16: LCM1602_IIC1.RW, LCD1.R/W
  N17: LCM1602_IIC1.E, LCD1.E
  N18: LCM1602_IIC1.D0, LCD1.DB0
  N19: LCM1602_IIC1.D1, LCD1.DB1
  N20: LCM1602_IIC1.D2, LCD1.DB2
  N21: LCM1602_IIC1.D3, LCD1.DB3
  N22: LCM1602_IIC1.D4, LCD1.DB4
  N23: LCM1602_IIC1.D5, LCD1.DB5
  N24: LCM1602_IIC1.D6, LCD1.DB6
  N25: LCM1602_IIC1.D7, LCD1.DB7
  N26: LCM1602_IIC1.A, LCD1.LED+
  N27: LCM1602_IIC1.K, LCD1.LED-
  N28: LCM1602_IIC1.LED_A, LCM1602_IIC1.LED_B

custom parts:
  Membran Keypad 4x4: Membrane Keypad 4x4 Matrix
  KY-019 5V Relay Module: 5V Relay module KEYES KY-019, used to control AC circuits.
  LCM1602 IIC: I2C-Module to use a 1602 or 2004 LCD on with the wire.h libory Serial LCD Modul

// code stored in the sketch: Untitled2.ino
#include <Keypad.h>
#include <EEPROM.h>
#include <Wire.h>
#include <LiquidCrystal_I2C.h>


LiquidCrystal_I2C lcd = LiquidCrystal_I2C(0x27, 16, 2);
char password[4];
char initial_password[4], new_password[4];
int vcc = 11;
int i = 0;
int relay_pin = 11;
char key_pressed = 0;
const byte rows = 4;
const byte columns = 4;
char hexaKeys[rows][columns] = {
  { '1', '2', '3', 'A' },
  { '4', '5', '6', 'B' },
  { '7', '8', '9', 'C' },
  { '*', '0', '#', 'D' }
};
byte row_pins[rows] = { 2, 3, 4, 5 };
byte column_pins[columns] = { 6, 7, 8, 9 };
Keypad keypad_key = Keypad(makeKeymap(hexaKeys), row_pins, column_pins, rows, columns);


void setup() {
  lcd.init();
  lcd.backlight();
  pinMode(relay_pin, OUTPUT);
  pinMode(vcc, OUTPUT);



  lcd.print("Bruce's Lock Box");
  lcd.setCursor(0, 1);
  lcd.print("   Keep Out!    ");
  delay(3000);
  lcd.clear();
  lcd.print("Speak friend,");
  lcd.setCursor(0, 1);
  lcd.print("and enter:");
  initialpassword();
}
void loop() {
  digitalWrite(relay_pin, HIGH);


  key_pressed = keypad_key.getKey();
  if (key_pressed == '#')
    change();
  if (key_pressed) {
    password[i++] = key_pressed;
    lcd.print("*");
  }
  if (i == 4) {
    delay(200);
    for (int j = 0; j < 4; j++)
      initial_password[j] = EEPROM.read(j);
    if (!(strncmp(password, initial_password, 4))) {
      lcd.clear();
      lcd.print("Keep it secret!");
      lcd.setCursor(0, 1);
      lcd.print("Keep it safe!");
      digitalWrite(relay_pin, LOW);
      delay(3000);
      lcd.setCursor(0, 0);
      lcd.clear();
      lcd.print("Press #");
      lcd.setCursor(0, 1);
      lcd.print("to change pass");
      delay(3000);
      lcd.clear();
      lcd.print("Speak friend,");
      lcd.setCursor(0, 1);
      lcd.print("and enter:");
      i = 0;
    } else {
      digitalWrite(relay_pin, HIGH);
      lcd.clear();
      lcd.print("Your words have");
      lcd.setCursor(0, 1);
      lcd.print("no power here.");
      lcd.setCursor(0, 0);
      delay(3000);
      lcd.clear();
      lcd.print("Speak friend,");
      lcd.setCursor(0, 1);
      lcd.print("and enter:");
      i = 0;
    }
  }
}



void change() {
  int j = 0;
  lcd.clear();
  lcd.print("Current Password");
  lcd.setCursor(0, 1);
  while (j < 4) {
    char key = keypad_key.getKey();
    if (key) {
      new_password[j++] = key;
      lcd.print("*");
    }
    key = 0;
  }
  delay(500);


  if ((strncmp(new_password, initial_password, 4))) {
    lcd.clear();
    lcd.print("      YOU!      ");
    delay(2000);
    lcd.clear();
    lcd.print("   SHALL NOT!   ");
    delay(2000);
    lcd.clear();
    lcd.print("    PASS!!!     ");
    delay(3000);
    lcd.clear();
  }


  else {
    j = 0;
    lcd.clear();
    lcd.print("New Password:");
    lcd.setCursor(0, 1);


    while (j < 4) {
      char key = keypad_key.getKey();
      if (key) {
        initial_password[j] = key;
        lcd.print(key);
        EEPROM.write(j, key);
        j++;
      }
    }
    delay(500);
    lcd.clear();
    lcd.print("Pass Changed");
    lcd.setCursor(0, 1);
    delay(1000);
  }


  lcd.clear();
  lcd.print("Speak friend,");
  lcd.setCursor(0, 1);
  lcd.print("and enter.");
  key_pressed = 0;
}


void initialpassword() {
  int j;
  for (j = 0; j < 4; j++)
    EEPROM.write(j, j + 49);
  for (j = 0; j < 4; j++)
    initial_password[j] = EEPROM.read(j);
}
