# Fritzing sketch motion_alarm (saved by Fritzing 0.9.10b)
circuit board: 8.46667cm x 5.64444cm
breadboards: 1

parts:
  Part1 = Arduino Uno (Rev3)
  LED1 = LED - 5mm [color="Red (633nm)" current=0.030 package="5 mm [THT]"]
  R2 = Resistor [tolerance=±5% power=0.25 resistance=220 package=THT]
  LED2 = LED - 5mm [color="Red (633nm)" current=0.030 package="5 mm [THT]"]
  LED3 = LED - 5mm [color="Red (633nm)" current=0.030 package="5 mm [THT]"]
  LED4 = LED - 5mm [color="Red (633nm)" current=0.030 package="5 mm [THT]"]
  LED5 = LED - 5mm [color="Red (633nm)" current=0.030 package="5 mm [THT]"]
  LED6 = LED - 5mm [color="Red (633nm)" current=0.030 package="5 mm [THT]"]
  HC-SR04_Sensor_1 = HC-SR04 Ultrasonic Distance Sensor
  R3 = Resistor [tolerance=±5% power=0.25 resistance=220 package=THT]
  R4 = Resistor [tolerance=±5% power=0.25 resistance=220 package=THT]
  R5 = Resistor [tolerance=±5% power=0.25 resistance=220 package=THT]
  R6 = Resistor [tolerance=±5% power=0.25 resistance=220 package=THT]
  R7 = Resistor [tolerance=±5% power=0.25 resistance=220 package=THT]
  J1 = Piezo Speaker

nets:
  N1: Part1.D9_PWM, HC-SR04_Sensor_1.TRIG
  N2: Part1.D10_PWM/SS, HC-SR04_Sensor_1.ECHO
  N3: Part1.D11_PWM/MOSI, J1.pin2
  GND: Part1.GND, R2.Pin_1, HC-SR04_Sensor_1.GND, R3.Pin_1, R4.Pin_1, R5.Pin_1, R6.Pin_1, R7.Pin_1, J1.pin1
  N4: Part1.D2, LED1.anode
  N5: Part1.D3_PWM, LED2.anode
  N6: Part1.D4, LED3.anode
  N7: Part1.D5_PWM, LED4.anode
  N8: Part1.D6_PWM, LED5.anode
  N9: Part1.D7, LED6.anode
  5V: Part1.5V, HC-SR04_Sensor_1.VCC
  N10: LED1.cathode, R2.Pin_0
  N11: LED2.cathode, R3.Pin_0
  N12: LED3.cathode, R4.Pin_0
  N13: LED4.cathode, R5.Pin_0
  N14: LED5.cathode, R6.Pin_0
  N15: LED6.cathode, R7.Pin_0

notes:
  [write your nere]
  e]
